# Fritzing sketch Schaltplan (saved by Fritzing 0.9.10b)
breadboards: 2

parts:
  part = Raspberry Pi 4B
  Ultraschallsensor_Rechts = HC-SR04 Ultrasonic Distance Sensor
  Ultraschallsensor_Hinten = HC-SR04 Ultrasonic Distance Sensor
  Ultraschallsensor_Links = HC-SR04 Ultrasonic Distance Sensor
  U1 = L298_BRIDGE_DRIVER [package=powerso20]
  part_2 = Basic Servo
  Spannung_18V = Power plug [part_number="DC Input"]
  Knopf = Momentary Switch [package=ksa_sealed_tac_switch]
  LED = LED - 5mm [color="Red (633nm)" current=0.030 package="5 mm [THT]"]
  Motor = DC Motor [voltage_(max)=6V voltage_(min)=3V]
  Farbsensor = Adafruit TCS34725 RGB Color Sensor [part_number="Adafruit #1334"]
  part_3 = Raspberry Pi 4B
  C1 = Tantalum Capacitor [capacitance=1μF voltage=35V package="100 mil [THT, tantalum]"]  # not connected
  LED_2 = LED - 5mm [color="Red (633nm)" current=0.030 package="5 mm [THT]"]
  Schalter = Taiway 100-SP-X-T1 SPDT Miniature Toggle Switch [part_number=100-SP-X-T1-0-0-B1-M2 package=THT]
  part_4 = Voltage Regulator [package=to220-igo]
  Ultraschallsensor_Vorne = HC-SR04 Ultrasonic Distance Sensor
  Gyrosensor = InvenSense MPU6050

nets (from the schematic view):
  3V3: part.3V3, Gyrosensor.VCC
  VCC: part.5V, Ultraschallsensor_Rechts.VCC, Ultraschallsensor_Hinten.VCC, Ultraschallsensor_Links.VCC, part_2.vcc, part_3.5V, Schalter.L1, Ultraschallsensor_Vorne.VCC
  N1: part.GPIO2, Gyrosensor.SDA
  N2: part.GPIO3, Gyrosensor.SCL
  GND: part.GND, Ultraschallsensor_Rechts.GND, Ultraschallsensor_Hinten.GND, Ultraschallsensor_Links.GND, U1.GND, part_2.gnd, Spannung_18V.GND, Knopf.1, LED.anode, Farbsensor.GND, part_3.GND, LED_2.anode, part_4.GND, Ultraschallsensor_Vorne.GND, Gyrosensor.GND
  N3: part.GPIO17, part_2.pulse
  N4: part.GPIO18, Ultraschallsensor_Vorne.TRIG
  N5: part.GPIO27, Ultraschallsensor_Rechts.TRIG
  N6: part.GPIO22, Ultraschallsensor_Rechts.ECHO
  N7: part.GPIO23, U1.IN3
  N8: part.GPIO24, U1.ENB
  N9: part.GPIO25, U1.IN4
  N10: part.GPIO8, Ultraschallsensor_Vorne.ECHO
  N11: part.GPIO7, Knopf.3
  N12: part.GPIO5, part_3.GPIO5
  N13: part.GPIO6, part_3.GPIO11
  N14: part.GPIO12, LED.cathode
  N15: part.GPIO13, part_3.GPIO9
  N16: part.GPIO19, Ultraschallsensor_Links.ECHO
  N17: part.GPIO26, Ultraschallsensor_Links.TRIG
  N18: part.GPIO20, Ultraschallsensor_Hinten.ECHO
  N19: part.GPIO21, Ultraschallsensor_Hinten.TRIG
  N20: U1.OUT1, Motor.pin_1
  N21: U1.OUT2, Motor.pin_2
  N22: U1.SENSE_B, Spannung_18V.VCC, part_4.IN
  +3V3: Farbsensor.+3V3, part_3.3V3
  N23: Farbsensor.SCL, part_3.GPIO3
  N24: Farbsensor.SDA, part_3.GPIO2
  N25: part_3.GPIO12, LED_2.cathode
  N26: Schalter.COM, part_4.OUT

notes:
  Rot: 5V
  Orange: 18V
  Schwarz: Gnd
  Gelb: Servo Daten
  Cyan: Ultraschall Trig
  Ocker: Ultraschall Echo
  Grau: Led / Button
  Grün: Ultraschallverlängerungen
  Kamera

custom parts:
  Adafruit TCS34725 RGB Color Sensor: Your electronics can now see in dazzling color with this lovely color light sensor. We found the best color sensor on the market, the TCS34725, which has RGB and Clear light sensing elements. An IR blocking filter, integrated on-chip and localized to the color sensing photodiodes, minimizes the IR spectral component of the incoming light and allows color measurements to be made accurately. The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
