# Fritzing sketch Steckplatine (saved by Fritzing 0.9.10b)

parts:
  Mod1 = Raspberry Pi 4B
  HC-SR04_Sensor_3 = HC-SR04 Ultrasonic Distance Sensor
  HC-SR04_Sensor_4 = HC-SR04 Ultrasonic Distance Sensor
  HC-SR04_Sensor_5 = HC-SR04 Ultrasonic Distance Sensor
  S2 = Momentary Switch [package=ksa_sealed_tac_switch]
  LED1 = LED - 5mm [color="Red (633nm)" current=0.030 package="5 mm [THT]"]
  IC7 = Voltage Regulator [package=to220-igo]
  Input1 = Power plug [part_number="DC Input"]
  M1 = DC Motor [voltage_(max)=6V voltage_(min)=3V]
  J1 = Basic Servo
  S4 = H-Bridge with L298N
  Bauteil1 = Adafruit TCS34725 RGB Color Sensor [part_number="Adafruit #1334"]
  Mod2 = Raspberry Pi 4B
  Bauteil2 = InvenSense MPU6050
  LED3 = smd LED [color="Red (633nm)" package="0603 [SMD]"]
  S5 = Taiway 100-SP-X-T1 SPDT Miniature Toggle Switch [part_number=100-SP-X-T1-0-0-B1-M2 package=THT]
  HC-SR04_Sensor_6 = HC-SR04 Ultrasonic Distance Sensor

nets (from the breadboard view):
  3V3: Mod1.3V3, Mod1.GPIO22, HC-SR04_Sensor_5.ECHO, Bauteil2.VCC
  VCC: Mod1.5V, HC-SR04_Sensor_3.VCC, HC-SR04_Sensor_4.VCC, HC-SR04_Sensor_5.VCC, J1.vcc, Mod2.5V, S5.L1, HC-SR04_Sensor_6.VCC
  N1: Mod1.GPIO2, Bauteil2.SDA
  N2: Mod1.GPIO3, Bauteil2.SCL
  GND: Mod1.GND, Mod1.GPIO14, Mod1.GPIO24, HC-SR04_Sensor_3.GND, HC-SR04_Sensor_4.GND, HC-SR04_Sensor_5.GND, S2.2, LED1.anode, IC7.GND, Input1.GND, J1.gnd, S4.GND, S4.IN4, Bauteil1.GND, Bauteil2.GND, HC-SR04_Sensor_6.GND
  N3: Mod1.GPIO17, J1.pulse
  N4: Mod1.GPIO18, HC-SR04_Sensor_6.TRIG
  N5: Mod1.GPIO27, HC-SR04_Sensor_5.TRIG
  N6: Mod1.GPIO23, S4.IN3
  N7: Mod1.GPIO25, Mod1.GPIO8, S4.ENB, HC-SR04_Sensor_6.ECHO
  N8: Mod1.GPIO7, S2.3
  N9: Mod1.GPIO5, Mod2.GPIO5
  N10: Mod1.GPIO6, Mod2.GPIO11
  N11: Mod1.GPIO12, LED1.cathode
  N12: Mod1.GPIO13, Mod2.GPIO9
  N13: Mod1.GPIO19, HC-SR04_Sensor_4.ECHO
  N14: Mod1.GPIO26, HC-SR04_Sensor_4.TRIG
  N15: Mod1.GPIO20, HC-SR04_Sensor_3.ECHO
  N16: Mod1.GPIO21, HC-SR04_Sensor_3.TRIG
  VCC_2: IC7.IN, Input1.VCC, S4.12V
  N17: IC7.OUT, S5.L2
  N18: M1.pin_1, S4.M1-02
  N19: M1.pin_2, S4.M1-01
  +3V3: Bauteil1.+3V3, Mod2.3V3
  N20: Bauteil1.SCL, Mod2.GPIO3
  N21: Bauteil1.SDA, Mod2.GPIO2
  N22: Mod2.GND, LED3.anode
  N23: Mod2.GPIO12, LED3.cathode

notes:
  Kamera

custom parts:
  H-Bridge with L298N: h-bridge
  Adafruit TCS34725 RGB Color Sensor: Your electronics can now see in dazzling color with this lovely color light sensor. We found the best color sensor on the market, the TCS34725, which has RGB and Clear light sensing elements. An IR blocking filter, integrated on-chip and localized to the color sensing photodiodes, minimizes the IR spectral component of the incoming light and allows color measurements to be made accurately. The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
